# Fritzing sketch WaterBot (saved by Fritzing 0.9.3b)
breadboards: 1

parts:
  U1 = 2-Channel 5v Relay Shield [package=relay-2ch5v10a]
  Part4 = FC-28 Soil Hygrometer Module - Probe
  Part2 = Adafruit Feather HUZZAH ESP8266 [part_number="Adafruit #2821"]
  Power_plug1 = Power plug
  M1 = DC Motor
  LED1 = smd LED [color="Blue (430nm)" package="0603 [SMD]"]
  Part6 = FC-28 Soil Hygrometer Module
  Part7 = FC-28 Soil Hygrometer Module - Probe
  Part5 = Adafruit OLED FeatherWing [part_number="Adafruit #2900"]
  Part9 = Logic Level Converter
  Part3 = FC-28 Soil Hygrometer Module
  R1 = Resistor [tolerance=±5% resistance=270 package=THT]
  R2 = Resistor [tolerance=±5% resistance=120 package=THT]

nets:
  N1: U1.VCC, Part2.VBUS, Part9.HV
  GND: U1.GND, Part2.GND, Part6.GND, Part9.GND, Part3.GND, R2.Pin_1
  N2: U1.IN1, Part9.TX2_HV
  N3: U1.IN2, Part9.TX_HV
  N4: U1.K1-In, U1.K2-In, Power_plug1.VCC
  N5: U1.K1-On, M1.pin_1
  N6: U1.K2-On, LED1.cathode
  N7: Part4.POS, Part3.POS
  N8: Part4.NEG, Part3.NEG
  N9: Part2.GPIO12/MISO, Part6.DO
  N10: Part2.GPIO13/MOSI, Part3.DO
  N11: Part2.GPIO14/SCK, Part9.TX_LV
  N12: Part2.ADC, R1.Pin_0, R2.Pin_0
  N13: Part2.3.3V, Part9.LV
  N14: Part2.RESET, Part5.!RESET
  N15: Part2.GPIO15, Part9.TX2_LV
  VCC: Part2.GPIO0, Part6.VCC, Part5.J, Part3.VCC
  N16: Part2.GPIO16, Part5.I
  N17: Part2.GPIO2, Part5.H
  N18: Part2.GPIO5/SCL, Part5.SCL
  N19: Part2.GPIO4/SDA, Part5.SDA
  N20: Power_plug1.GND, M1.pin_2, LED1.anode
  N21: Part6.POS, Part7.POS
  N22: Part6.NEG, Part7.NEG
  N23: Part3.AO, R1.Pin_1

notes:
  Supply Water Level
  Tree Water Level
  Status Indicator
  12VDC Supply
  WaterBot 1.1
  Pump
  2018
  UART
  // Serial Interfaces
  // 1 - SER - Serial Monitor TX
  // 3 - SER - Serial Monitor RX
  // 4 - I2C - SDA OLED Display
  // 5 - I2C - SCL OLED Display
  // Sensors
  // 0 - DOUT - Sensor Excitation / Red LED
  // 12 - DIN - Supply Level (Binary)
  // 13 - DIN - Tree Level (Binary)
  // A0 - AIN - Tree Level (Analog)
  // Switched Voltage Outputs
  // 2 - DOUT - Tree LED (switched 12V) / Blue LED
  // 15 - DOUT - Pump Power (switched 12V)
  // Physical Pushbuttons
  // 16 - DIN - Button B
  Blue LED
  Solid - Monitoring
  Slow - Pumping
  Fast - Supply Reservoir Empty
  Off - Sleep Mode

custom parts:
  2-Channel 5v Relay Shield: 2 Channel 5v Relay Shield w. 2x SPD-06VDC-SD-C
  FC-28 Soil Hygrometer Module - Probe: The FC-28 is a soil hygrometer module that uses the Texas Instruments LM393 comparator chip to provide an analog measurement of soil humidity.
  Adafruit Feather HUZZAH ESP8266: his is the Adafruit Feather HUZZAH ESP8266 - our take on an 'all-in-one' ESP8266 WiFi development board with built in USB and battery charging. Its an ESP8266 WiFi module with all the extras you need, ready to rock! We have other boards in the Feather family, check'em out here. At the Feather HUZZAH's heart is an ESP8266 WiFi microcontroller clocked at 80 MHz and at 3.3V logic. This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
  FC-28 Soil Hygrometer Module: The FC-28 is a soil hygrometer module that uses the Texas Instruments LM393 comparator chip to provide an analog measurement of soil humidity. The digital output is high when soil moisture is over a certain threshold, as determined by adjusting the potentiometer.
  Adafruit OLED FeatherWing: This is the FeatherWing OLED: it adds a 128x32 monochrome OLED plus 3 user buttons to any Feather main board. These displays are small, only about 1" diagonal, but very readable due to the high contrast of an OLED display. This screen is made of 128x32 individual white OLED pixels and because the display makes its own light, no backlight is required. This reduces the power required to run the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
